// Logisim project 1 bit memory.circ as structural Verilog
module Active_Low_SR_latch (
  input  s,
  input  r,
  output q,
  output nq
);

  nand nand_1 (q, s, nq);
  nand nand_2 (nq, q, r);

  // Notes on the sheet:
  //   Active Low S R Latch
endmodule

module Active_High_with_Enable (
  input  s,
  input  e,
  input  r,
  output q,
  output nq
);

  wire nand_1_out, nand_2_out;

  nand nand_1 (nand_1_out, s, e);
  nand nand_2 (nand_2_out, e, r);
  nand nand_3 (q, nand_1_out, nq);
  nand nand_4 (nq, q, nand_2_out);

  // Notes on the sheet:
  //   Active High with Enable
endmodule

module Active_High_with_Enable_2 (
  input  s,
  input  e,
  output q,
  output nq
);

  wire nand_1_out, nand_2_out, not_1_out;

  not not_1 (not_1_out, s);
  nand nand_1 (nand_1_out, s, e);
  nand nand_2 (nand_2_out, e, not_1_out);
  nand nand_3 (q, nand_1_out, nq);
  nand nand_4 (nq, q, nand_2_out);

  // Notes on the sheet:
  //   Active High with Enable
endmodule

module CPU_MEM_1 (
  input  s,
  input  e,
  output q
);

  wire nand_1_out, nand_2_out, nand_4_out;

  nand nand_1 (nand_1_out, s, e);
  nand nand_2 (nand_2_out, nand_1_out, e);
  nand nand_3 (q, nand_1_out, nand_4_out);
  nand nand_4 (nand_4_out, q, nand_2_out);

  // Notes on the sheet:
  //   1 Bit Memory
endmodule

module CPU_MEM_8 (
  input  [7:0] i,
  input  s,
  output [7:0] out_3
);

  CPU_MEM_1 cpu_mem_1_1 (.s(i[0]), .e(s), .q(out_3[0]));
  CPU_MEM_1 cpu_mem_1_2 (.s(i[1]), .e(s), .q(out_3[1]));
  CPU_MEM_1 cpu_mem_1_3 (.s(i[2]), .e(s), .q(out_3[2]));
  CPU_MEM_1 cpu_mem_1_4 (.s(i[3]), .e(s), .q(out_3[3]));
  CPU_MEM_1 cpu_mem_1_5 (.s(i[4]), .e(s), .q(out_3[4]));
  CPU_MEM_1 cpu_mem_1_6 (.s(i[5]), .e(s), .q(out_3[5]));
  CPU_MEM_1 cpu_mem_1_7 (.s(i[6]), .e(s), .q(out_3[6]));
  CPU_MEM_1 cpu_mem_1_8 (.s(i[7]), .e(s), .q(out_3[7]));
endmodule

module CPU_ENABLE (
  input  [7:0] i,
  input  e,
  output [7:0] o
);

  and and_1 (o[0], i[0], e);
  and and_2 (o[1], i[1], e);
  and and_3 (o[2], i[2], e);
  and and_4 (o[3], i[3], e);
  and and_5 (o[4], i[4], e);
  and and_6 (o[5], i[5], e);
  and and_7 (o[6], i[6], e);
  and and_8 (o[7], i[7], e);
endmodule

module CPU_ERG_8 (
  input  [7:0] i,
  input  s,
  input  e,
  output [7:0] o
);

  wire [7:0] cpu_mem_8_1_out_3;

  CPU_MEM_8 cpu_mem_8_1 (.i(i), .out_3(cpu_mem_8_1_out_3), .s(s));
  CPU_ENABLE cpu_enable_1 (.i(cpu_mem_8_1_out_3), .o(o), .e(e));
endmodule
