// Logisim project build cpu.circ as structural Verilog: 3 circuits, main circuit main
module main (
);

  NAND nand_1 ();  // open: in_1, out_3, in_2
  NAND nand_2 ();  // open: in_1, out_3, in_2
  C1 c1_1 ();  // open: i, out_2
  C1 c1_2 ();  // open: i, out_2
endmodule

module NAND (
  input  in_1,
  input  in_2,
  output out_3
);

  wire and_1_out;

  and and_1 (and_1_out, in_1, in_2);
  not not_1 (out_3, and_1_out);
endmodule

module C1 (
  input  [7:0] i,
  output out_2
);

  wire nand_1_out_3, nand_2_out_3, nand_3_out_3, nand_4_out_3;

  NAND nand_1 (.in_1(i[0]), .out_3(nand_1_out_3), .in_2(i[1]));
  NAND nand_2 (.in_1(i[2]), .out_3(nand_2_out_3), .in_2(i[3]));
  NAND nand_3 (.in_1(i[4]), .out_3(nand_3_out_3), .in_2(i[5]));
  NAND nand_4 (.in_1(i[6]), .out_3(nand_4_out_3), .in_2(i[7]));
  nor nor_1 (out_2, nand_1_out_3, nand_2_out_3, nand_3_out_3, nand_4_out_3);
endmodule
